// Logisim project HalfAdder.circ as structural Verilog: 1 circuit, main circuit main
module main (
  input  A,
  input  B
);

  wire and_1_out, and_2_out, not_1_out, or_1_out;

  or or_1 (or_1_out, A, B);
  and and_1 (and_1_out, A, B);
  not not_1 (not_1_out, and_1_out);
  and and_2 (and_2_out, or_1_out, not_1_out);
  LED led_1 (.in(and_2_out));
  LED led_2 (.in(and_1_out));

  // Notes on the sheet:
  //   SUM
  //   CARRY
endmodule
