// Logisim project Lab 2 C Circuit.circ as structural Verilog: 1 circuit, main circuit main
module main (
  input  B,
  input  C,
  input  D
);

  wire not_1_out, or_1_out, or_2_out;

  not not_1 (not_1_out, C);
  or or_1 (or_1_out, not_1_out, D);
  LED led_1 (.in(or_2_out));
  or or_2 (or_2_out, B, or_1_out);
endmodule
