// Logisim project Lab 2 E Circuit.circ as structural Verilog: 1 circuit, main circuit main
module main (
  input  B,
  input  C,
  input  D
);

  wire and_1_out, and_2_out, not_1_out, not_2_out, or_1_out;

  not not_1 (not_1_out, B);
  not not_2 (not_2_out, D);
  and and_1 (and_1_out, not_1_out, not_2_out);
  and and_2 (and_2_out, C, not_2_out);
  or or_1 (or_1_out, and_1_out, and_2_out);
  LED led_1 (.in(or_1_out));

  // Notes on the sheet:
  //   e
endmodule
