// Logisim project Lab 2 G Circuit.circ as structural Verilog: 1 circuit, main circuit main
module main (
  input  B,
  input  C,
  input  D
);

  wire and_1_out, and_2_out, and_3_out, not_1_out, not_2_out, not_3_out, or_1_out, or_2_out;

  not not_1 (not_1_out, B);
  not not_2 (not_2_out, C);
  not not_3 (not_3_out, D);
  and and_1 (and_1_out, not_2_out, B);
  and and_2 (and_2_out, not_1_out, C);
  and and_3 (and_3_out, C, not_3_out);
  or or_1 (or_1_out, and_1_out, and_2_out);
  LED led_1 (.in(or_2_out));
  or or_2 (or_2_out, or_1_out, and_3_out);

  // Notes on the sheet:
  //   g
endmodule
